// Digital circuit examen_controller.dig as structural Verilog
module examen_controller (
  input  [31:0] address,
  input  [19:0] mtag0,
  input  [19:0] mtag1,
  input  [31:0] data0,
  input  [31:0] data1,
  input  mvalid0,
  input  mvalid1,
  input  [31:0] mword0w0,
  input  [31:0] mword1w0,
  input  [31:0] mword0w1,
  input  [31:0] mword1w1,
  output [8:0] index,
  output hit,
  output [31:0] data
);

  wire and1, and2, comparador1, comparador2, \priority ;

  Comparator #(.Bits(20)) comparator_1 (.a(address[31:12]), .b(mtag0), .eq(comparador1));  // open: gt, lt
  Comparator #(.Bits(20)) comparator_2 (.a(address[31:12]), .b(mtag1), .eq(comparador2));  // open: gt, lt
  and and_1 (and1, comparador1, mvalid0);
  and and_2 (and2, comparador2, mvalid1);
  or or_1 (hit, and1, and2);
  Multiplexer #(.Bits(32)) multiplexer_1 (.sel(address[2]), .in_0(mword0w0), .in_1(mword1w0));  // open: out
  Multiplexer #(.Bits(32)) multiplexer_2 (.sel(address[2]), .in_0(mword0w1), .in_1(mword1w1));  // open: out
  PriorityEncoder priorityencoder_1 (.in0(and1), .in1(and2), .num(\priority ));  // open: any
  Multiplexer #(.Bits(32)) multiplexer_3 (.sel(\priority ), .in_0(data0), .in_1(data1), .out(data));

  assign index = address[11:3];

  // Other names for the same wires on the sheet: noname[1:0] = address[1:0]; word_offset = address[2];
  //   tag[19:0] = address[31:12]

  // Notes on the sheet:
  //   Me perdi al agregarla las 2 palabras
  //   a las memorias :/
  //   GRACIAS
endmodule
